// Logisim project TaskOne.circ as structural Verilog: 2 circuits, main circuit OneBitSubtraction
module OneBitSubtraction (
  input  A,
  input  B,
  input  Cin,
  output Cout,
  output Result
);

  wire aB_out, Abc_out, aBci_out, abCIN_out, ABCINT_out, aCIN_out, BCIN_out, not_1_out, not_2_out, not_3_out;

  not not_1 (not_1_out, A);
  not not_2 (not_2_out, B);
  not not_3 (not_3_out, Cin);
  and aCIN (aCIN_out, not_1_out, Cin);
  and aB (aB_out, not_1_out, B);
  and BCIN (BCIN_out, B, Cin);
  and abCIN (abCIN_out, not_1_out, not_2_out, Cin);
  and aBci (aBci_out, not_1_out, B, not_3_out);
  and Abc (Abc_out, A, not_2_out, not_3_out);
  and ABCINT (ABCINT_out, A, B, Cin);
  or or_1 (Cout, aCIN_out, aB_out, BCIN_out);
  or or_2 (Result, abCIN_out, aBci_out, Abc_out, ABCINT_out);
endmodule

module TaskOne (
  input  in_1,
  input  [7:0] A,
  input  [7:0] B,
  output [7:0] Result,
  output out_5
);

  wire onebitsubtraction_1_cout, onebitsubtraction_2_cout, onebitsubtraction_3_cout,
       onebitsubtraction_4_cout, onebitsubtraction_5_cout, onebitsubtraction_6_cout, onebitsubtraction_7_cout;

  OneBitSubtraction onebitsubtraction_1 (
    .A(A[0]), .B(B[0]), .Cin(in_1), .Cout(onebitsubtraction_1_cout), .Result(Result[0]));
  OneBitSubtraction onebitsubtraction_2 (
    .A(A[1]), .B(B[1]), .Cin(onebitsubtraction_1_cout), .Cout(onebitsubtraction_2_cout), .Result(Result[1]));
  OneBitSubtraction onebitsubtraction_3 (
    .A(A[2]), .B(B[2]), .Cin(onebitsubtraction_2_cout), .Cout(onebitsubtraction_3_cout), .Result(Result[2]));
  OneBitSubtraction onebitsubtraction_4 (
    .A(A[3]), .B(B[3]), .Cin(onebitsubtraction_3_cout), .Cout(onebitsubtraction_4_cout), .Result(Result[3]));
  OneBitSubtraction onebitsubtraction_5 (
    .A(A[4]), .B(B[4]), .Cin(onebitsubtraction_4_cout), .Cout(onebitsubtraction_5_cout), .Result(Result[4]));
  OneBitSubtraction onebitsubtraction_6 (
    .A(A[5]), .B(B[5]), .Cin(onebitsubtraction_5_cout), .Cout(onebitsubtraction_6_cout), .Result(Result[5]));
  OneBitSubtraction onebitsubtraction_7 (
    .A(A[6]), .B(B[6]), .Cin(onebitsubtraction_6_cout), .Cout(onebitsubtraction_7_cout), .Result(Result[6]));
  OneBitSubtraction onebitsubtraction_8 (
    .A(A[7]), .B(B[7]), .Cin(onebitsubtraction_7_cout), .Cout(out_5), .Result(Result[7]));
endmodule
