// Logisim project TaskThree.circ as structural Verilog: 1 circuit, main circuit main
module main (
  output out_1,
  output out_2,
  output out_3,
  output out_4
);

  wire clock_1_out, nand_1_out, nand_2_out, not_1_out, not_2_out, t_ff_1_qn, t_ff_2_qn, t_ff_3_qn, t_ff_4_qn;

  LED led_1 (.in(out_1));
  T_Flip_Flop t_ff_1 (.T(not_1_out), .clk(clock_1_out), .Q(out_1), .Qn(t_ff_1_qn));  // open: reset, preset
  LED led_2 (.in(out_2));
  T_Flip_Flop t_ff_2 (.T(not_2_out), .clk(clock_1_out), .Q(out_2), .Qn(t_ff_2_qn));  // open: reset, preset
  Clock clock_1 (.out(clock_1_out));
  LED led_3 (.in(out_3));
  T_Flip_Flop t_ff_3 (.T(t_ff_4_qn), .clk(clock_1_out), .Q(out_3), .Qn(t_ff_3_qn));  // open: reset, preset
  nand nand_1 (nand_1_out, not_2_out, t_ff_2_qn);
  LED led_4 (.in(out_4));
  T_Flip_Flop t_ff_4 (.T(1'b1), .clk(clock_1_out), .Q(out_4), .Qn(t_ff_4_qn));  // open: reset, preset
  not not_1 (not_1_out, nand_1_out);
  nand nand_2 (nand_2_out, t_ff_4_qn, t_ff_3_qn);
  not not_2 (not_2_out, nand_2_out);
endmodule
