// Logisim project TaskTwo.circ as structural Verilog: 3 circuits, main circuit TaskTwo
module BCDdecoder (
  input  a,
  input  b,
  input  c,
  input  d,
  output x,
  output y,
  output z,
  output u
);

  wire and_2_out, and_3_out, and_4_out, and_5_out, and_6_out, and_7_out, and_8_out, and_9_out, not_1_out,
       not_2_out, not_3_out, not_4_out;

  not not_1 (not_1_out, a);
  not not_2 (not_2_out, b);
  not not_3 (not_3_out, c);
  not not_4 (not_4_out, d);
  and and_1 (x, a, b, c);
  and and_2 (and_2_out, b, not_3_out, not_4_out);
  and and_3 (and_3_out, a, not_2_out, c, d);
  and and_4 (and_4_out, a, b, not_3_out);
  and and_5 (and_5_out, not_1_out, not_2_out, c);
  and and_6 (and_6_out, a, b, not_3_out);
  and and_7 (and_7_out, not_1_out, not_2_out, d);
  and and_8 (and_8_out, a, b, d);
  and and_9 (and_9_out, not_2_out, c, d);
  or or_1 (y, and_2_out, and_3_out, and_4_out);
  or or_2 (z, and_5_out, and_6_out);
  or or_3 (u, and_7_out, and_8_out, and_9_out);
endmodule

module BCDencoder (
  input  a,
  input  b,
  input  c,
  input  d,
  input  e,
  output x,
  output y,
  output z,
  output u,
  output v,
  output w
);

  wire and_1_out, and_2_out, and_3_out, and_4_out, and_5_out, and_6_out, and_7_out, and_8_out, and_9_out,
       and_10_out, and_11_out, and_12_out, and_13_out, and_14_out, and_15_out, and_16_out, and_17_out,
       and_18_out, and_19_out, and_20_out, and_21_out, and_22_out, and_23_out, and_24_out, and_25_out,
       and_26_out, and_27_out, and_28_out, and_29_out, not_1_out, not_2_out, not_3_out, not_4_out, not_5_out;

  not not_1 (not_1_out, a);
  not not_2 (not_2_out, b);
  not not_3 (not_3_out, c);
  not not_4 (not_4_out, d);
  not not_5 (not_5_out, e);
  and and_1 (and_1_out, a, c);
  and and_2 (and_2_out, a, b);
  and and_3 (and_3_out, a, not_2_out, not_3_out);
  and and_4 (and_4_out, not_1_out, b, d);
  and and_5 (and_5_out, not_1_out, b, c);
  and and_6 (and_6_out, b, c, d);
  and and_7 (and_7_out, not_1_out, not_2_out, c, e);
  and and_8 (and_8_out, not_1_out, not_2_out, c, d);
  and and_9 (and_9_out, not_1_out, b, not_3_out, not_4_out);
  and and_10 (and_10_out, a, not_2_out, not_3_out);
  and and_11 (and_11_out, a, not_3_out, d);
  and and_12 (and_12_out, a, b, c, not_4_out);
  and and_13 (and_13_out, a, not_3_out, e);
  and and_14 (and_14_out, not_1_out, c, d, e);
  and and_15 (and_15_out, not_1_out, not_2_out, c, not_5_out);
  and and_16 (and_16_out, not_1_out, not_2_out, c, d);
  and and_17 (and_17_out, not_1_out, b, not_3_out, not_4_out);
  and and_18 (and_18_out, not_1_out, c, d, not_5_out);
  and and_19 (and_19_out, a, not_2_out, not_3_out);
  and and_20 (and_20_out, a, not_3_out, d);
  and and_21 (and_21_out, a, b, c, not_4_out);
  and and_22 (and_22_out, a, not_3_out, not_5_out);
  and and_23 (and_23_out, not_2_out, not_3_out, d);
  and and_24 (and_24_out, not_1_out, c, not_4_out, e);
  and and_25 (and_25_out, not_1_out, b, not_4_out);
  and and_26 (and_26_out, not_1_out, b, c, e);
  and and_27 (and_27_out, a, not_2_out, d);
  and and_28 (and_28_out, b, not_4_out, e);
  and and_29 (and_29_out, b, c, not_4_out);
  or or_1 (x, and_1_out, and_2_out);
  or or_2 (y, and_3_out, and_4_out, and_5_out, and_6_out);
  or or_3 (z, and_7_out, and_8_out, and_9_out, and_10_out, and_11_out, and_12_out, and_13_out, and_14_out);
  or or_4 (u, and_15_out, and_16_out, and_17_out, and_18_out, and_19_out, and_20_out, and_21_out, and_22_out);
  or or_5 (v, and_23_out, and_24_out, and_25_out, and_26_out, and_27_out, and_28_out, and_29_out);

  assign w = e;
endmodule

module TaskTwo (
  input  [3:0] in_1,
  input  [3:0] in_2,
  input  [3:0] in_3,
  output [1:0] out_4,
  output [3:0] out_5
);

  wire adder_1_cout, adder_2_cout, or_1_out;
  wire [3:0] adder_1_out, adder_2_out, bcddecoder_1_u, bcddecoder_2_u;

  BCDdecoder bcddecoder_1 (
    .a(in_1[3]), .b(in_1[2]), .c(in_1[1]), .d(in_1[0]), .x(bcddecoder_1_u[3]), .y(bcddecoder_1_u[2]),
    .z(bcddecoder_1_u[1]), .u(bcddecoder_1_u[0]));
  BCDdecoder bcddecoder_2 (
    .a(in_3[3]), .b(in_3[2]), .c(in_3[1]), .d(in_3[0]), .x(bcddecoder_2_u[3]), .y(bcddecoder_2_u[2]),
    .z(bcddecoder_2_u[1]), .u(bcddecoder_2_u[0]));
  Adder #(.width(4)) adder_1 (
    .a(bcddecoder_1_u), .b(bcddecoder_2_u), .out(adder_1_out), .cout(adder_1_cout));  // open: cin
  or or_1 (or_1_out, adder_1_cout, adder_2_cout);
  Adder #(.width(4)) adder_2 (.a(adder_1_out), .b(in_2), .out(adder_2_out), .cout(adder_2_cout));  // open: cin
  BCDencoder bcdencoder_1 (
    .a(or_1_out), .b(adder_2_out[3]), .c(adder_2_out[2]), .d(adder_2_out[1]), .e(adder_2_out[0]),
    .x(out_4[1]), .y(out_4[0]), .z(out_5[3]), .u(out_5[2]), .v(out_5[1]), .w(out_5[0]));
endmodule
